# Fritzing sketch Circuit connection (saved by Fritzing 0.9.3b)
circuit board: 8.46667cm x 5.64444cm
perfboards: 1
stripboards: 1

parts:
  Part1 = Arduino Uno (Rev3)
  J1 = Basic Servo
  J2 = Piezo Speaker
  S1 = Pushbutton [package="[THT]"]
  S2 = Pushbutton [package="[THT]"]
  FC-1 = Sound Sensor
  Water_Level_Sensor1 = Water Level Sensor

nets:
  N1: Part1.A0, Water_Level_Sensor1.SIG
  N2: Part1.D8, FC-1.OUT
  N3: Part1.D9_PWM, J1.pulse
  N4: Part1.D2, S2.Pin_1, S2.Pin_2
  N5: Part1.D3_PWM, S1.Pin_3, S1.Pin_4
  N6: Part1.D7, J2.pin2
  VCC: Part1.5V, J1.vcc, FC-1.VCC, Water_Level_Sensor1.VCC
  GND: Part1.GND, J1.gnd, J2.pin1, S1.Pin_1, S1.Pin_2, S2.Pin_3, S2.Pin_4, FC-1.GND, Water_Level_Sensor1.GND

custom parts:
  Water Level Sensor: A water level sensor. This sensor operates at 3V to 5V. The Sig (signal) pin outputs an analogue signal that is in proportion to the amount of water in contact with the sensor.
